# Fritzing sketch pull-up-counter (saved by Fritzing 0.9.10b)

parts:
  U1 = ESP32S-HiLetgo [part_number=ESP32S-HiLetgo]
  OLED_I2C1 = OLED 128x64 I2C Monochrome Display
  HC-SR04_Sensor_1 = HC-SR04 Ultrasonic Distance Sensor

nets:
  N1: U1.3.3, OLED_I2C1.VDD
  N2: U1.GPIO27, HC-SR04_Sensor_1.TRIG
  N3: U1.GPIO14, HC-SR04_Sensor_1.ECHO
  GND: U1.GND, OLED_I2C1.GND, HC-SR04_Sensor_1.GND
  VIN: U1.VIN, HC-SR04_Sensor_1.VCC
  N4: U1.GPIO21, OLED_I2C1.SDA
  N5: U1.GPIO22, OLED_I2C1.SCK

custom parts:
  ESP32S-HiLetgo: HiLetgo ESP-WROOM-32 ESP32 ESP-32S Development Board 2.4GHz Dual-Mode WiFi + Bluetooth Dual Cores Microcontroller The ESP32 integrated with Antenna switches, RF Balun, power amplifiers, low-noise amplifiers, filters, and management modules, and the entire solution occupies the least area of PCB. 2.4 GHz Wi-Fi plus Bluetooth dual-mode chip, with TSMC Ultra-low power consumption 40nm technology,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
